// Digital circuit Register.dig as structural Verilog
module Register (
  input  [15:0] In,
  output [15:0] Out
);

  wire bit_1_out;

  Bit bit_1 (.In(In[0]), .Out(bit_1_out));  // open: Load, Clock

  // Notes on the sheet:
  //   Register
endmodule
